# Fritzing sketch ganesh (1) (saved by Fritzing 0.9.6b)
circuit board: 8.46667cm x 5.64444cm
breadboards: 1

parts:
  R1 = Resistor [tolerance=±5% power=0.25 resistance=100k package=THT]
  R2 = Resistor [tolerance=±5% resistance=220k package="2512 [SMD]"]
  C1 = Ceramic Capacitor [capacitance=10nF voltage=63V package="100 mil [THT, multilayer]"]
  R3 = Resistor [tolerance=±5% resistance=12k package="2512 [SMD]"]
  R4 = Resistor [tolerance=±5% resistance=470k package="2512 [SMD]"]
  U2 = TRANSISTOR_NPN_2 [package=to-92]
  Q1 = PNP-Transistor [package="TO92 [THT]"]
  R5 = Resistor [tolerance=±5% resistance=1k package="2512 [SMD]"]
  R7 = Resistor [tolerance=±5% resistance=470k package="2512 [SMD]"]
  D1 = Rectifier Diode [part_number=1N4001 package="300 mil [THT]"]
  R8 = Photocell (LDR) [package=THT]
  D2 = Diode [package=diode-1n4001]
  D3 = Diode [package=diode-1n4001]
  D4 = Diode [package=diode-1n4001]
  D5 = Diode [package=diode-1n4001]
  TRM1 = Terminal 2pin
  JP1 = Header 2 [package=jst-2-smd-vert]

nets:
  N1: R1.Pin_0, D1.anode
  N2: R1.Pin_1, R2.Pin_0
  N3: R2.Pin_1, C1.0, R5.Pin_1, R7.Pin_1, D1.cathode, R8.pin_1, D4.C, D5.A
  N4: C1.1, R4.Pin_0
  N5: R3.Pin_1, U2.B
  N6: R4.Pin_1, U2.E
  N7: U2.C, R7.Pin_0
  N8: Q1.E, R5.Pin_0
  N9: Q1.B, Q1.C, R8.pin_0
  N10: D2.A, D4.A, TRM1.pin_2
  N11: D2.C, D3.C
  N12: D3.A, D5.C, JP1.1
  N13: TRM1.pin_1, JP1.2

custom parts:
  Terminal 2pin: 2-pin Terminal Block
